# Fritzing sketch emonth (saved by Fritzing 0.9.2b)
circuit board: 8.46667cm x 5.64444cm
breadboards: 1

parts:
  Arduino = Arduino Pro Mini v13
  ANT2 = Antenna
  C3 = Ceramic Capacitor [capacitance=100nF package="100 mil [THT, multilayer]"]
  battary = DC Power [voltage=5V]
  R4 = Resistor [tolerance=±5% resistance=4.7k package=THT]
  DHT22 = Humidity and Temperature Sensor RHT03
  DS18B20 = TEMPERATURE-SENSOR [package=to-92]
  RFM69CW = RFM12b HopeRF Transceiver
  R5 = Resistor [tolerance=±5% resistance=10k package=THT]

nets:
  3.3V: Arduino.VCC, C3.0, RFM69CW.9_VDD
  GND: Arduino.GND, C3.1, battary.V-, DHT22.GND_2, DS18B20.GND, RFM69CW.7_GND, RFM69CW.10_GND
  A4: Arduino.A4, DHT22.Data-signal, R5.Pin_1
  A5: Arduino.A5, R4.Pin_1, DS18B20.ADJ
  N1: Arduino.RAW, battary.V+
  D13: Arduino.D13/SCK, RFM69CW.13_SCK
  D12: Arduino.D12/MISO, RFM69CW.1_SDO
  D11: Arduino.D11_PWM/MOSI, RFM69CW.12_SDI
  D10: Arduino.D10_PWM/SS, RFM69CW.14_nSEL
  D6: Arduino.D6_PWM, DHT22.Vcc, R5.Pin_0
  D5: Arduino.D5_PWM, R4.Pin_0, DS18B20.VCC
  N2: ANT2.antenna_lead, RFM69CW.8_ANT
  D2: RFM69CW.2_nIRQ
